// Logisim project tsc8.circ as structural Verilog: 1 circuit, main circuit main
module main (
);

  wire and_1_out, and_2_out, and_3_out, and_4_out, and_5_out, and_6_out, and_7_out, and_8_out, and_9_out,
       button_1_out, clock_1_out, comparator_1_eq, comparator_2_eq, controlled_buffer_5_out, not_1_out,
       not_2_out, not_3_out, not_4_out, not_5_out, not_6_out, not_7_out, or_1_out, switch_1_p2, switch_2_p2,
       w65c02s_simple_1_p5;
  wire [6:0] controlled_buffer_3_out, keyboard_1_data;
  wire [7:0] controlled_buffer_10_out, ram_1_dout, rom_1_data, switch_18_p2, w65c02s_simple_1_p6;
  wire [7:7] controlled_buffer_3_out_2;
  wire [15:0] controlled_buffer_1_out, switch_25_p2, w65c02s_simple_1_p7;

  Button button_1 (.out(button_1_out));
  not not_1 (not_1_out, button_1_out);
  // Switch switch_1: pin names not known; wires that end beside it: 1'b1, switch_1_p2
  Clock clock_1 (.out(clock_1_out));
  and and_1 (and_1_out, 1'b1, not_1_out);
  Pull_Resistor pull_resistor_1 (.node(switch_1_p2));
  // Switch switch_2: pin names not known; wires that end beside it: 1'b1, switch_2_p2
  Pull_Resistor pull_resistor_2 (.node(switch_2_p2));
  and and_2 (and_2_out, clock_1_out, switch_1_p2);
  LED led_1 (.in(controlled_buffer_1_out[15]));
  LED led_2 (.in(controlled_buffer_1_out[14]));
  LED led_3 (.in(controlled_buffer_1_out[13]));
  LED led_4 (.in(controlled_buffer_3_out_2[7]));
  LED led_5 (.in(controlled_buffer_3_out[6]));
  LED led_6 (.in(controlled_buffer_3_out[5]));
  // Switch switch_3: pin names not known; wires that end beside it: 1'b1, switch_25_p2[15]
  Pull_Resistor pull_resistor_3 (.node(switch_25_p2[15]));
  // Switch switch_4: pin names not known; wires that end beside it: 1'b1, switch_18_p2[7], switch_18_p2[7]
  Pull_Resistor pull_resistor_4 (.node(switch_18_p2[7]));
  LED led_7 (.in(controlled_buffer_1_out[12]));
  LED led_8 (.in(controlled_buffer_1_out[11]));
  LED led_9 (.in(controlled_buffer_1_out[10]));
  LED led_10 (.in(controlled_buffer_1_out[9]));
  LED led_11 (.in(controlled_buffer_3_out[4]));
  LED led_12 (.in(controlled_buffer_3_out[3]));
  LED led_13 (.in(controlled_buffer_3_out[2]));
  LED led_14 (.in(controlled_buffer_3_out[1]));
  // Switch switch_5: pin names not known; wires that end beside it: 1'b1, switch_25_p2[14]
  // Switch switch_6: pin names not known; wires that end beside it: 1'b1, switch_25_p2[13]
  Pull_Resistor pull_resistor_5 (.node(switch_25_p2[14]));
  Pull_Resistor pull_resistor_6 (.node(switch_25_p2[13]));
  // Switch switch_7: pin names not known; wires that end beside it: 1'b1, switch_18_p2[6], switch_18_p2[6]
  // Switch switch_8: pin names not known; wires that end beside it: 1'b1, switch_18_p2[5], switch_18_p2[5]
  Pull_Resistor pull_resistor_7 (.node(switch_18_p2[6]));
  Pull_Resistor pull_resistor_8 (.node(switch_18_p2[5]));
  // W65C02S__Simple w65c02s_simple_1: pin names not known; wires that end beside it: and_2_out, 1'b0, 1'b0, and_1_out, w65c02s_simple_1_p5, w65c02s_simple_1_p6, w65c02s_simple_1_p7
  LED led_15 (.in(controlled_buffer_1_out[8]));
  LED led_16 (.in(controlled_buffer_1_out[7]));
  LED led_17 (.in(controlled_buffer_1_out[6]));
  LED led_18 (.in(controlled_buffer_1_out[5]));
  LED led_19 (.in(controlled_buffer_3_out[0]));
  // Switch switch_9: pin names not known; wires that end beside it: 1'b1, switch_25_p2[12]
  Pull_Resistor pull_resistor_9 (.node(switch_25_p2[12]));
  // Switch switch_10: pin names not known; wires that end beside it: 1'b1, switch_18_p2[4], switch_18_p2[4]
  Pull_Resistor pull_resistor_10 (.node(switch_18_p2[4]));
  LED led_20 (.in(controlled_buffer_1_out[4]));
  LED led_21 (.in(controlled_buffer_1_out[3]));
  LED led_22 (.in(controlled_buffer_1_out[2]));
  LED led_23 (.in(controlled_buffer_1_out[1]));
  // Switch switch_11: pin names not known; wires that end beside it: 1'b1, switch_25_p2[11]
  // Switch switch_12: pin names not known; wires that end beside it: 1'b1, switch_25_p2[10]
  Pull_Resistor pull_resistor_11 (.node(switch_25_p2[11]));
  Pull_Resistor pull_resistor_12 (.node(switch_25_p2[10]));
  // Switch switch_13: pin names not known; wires that end beside it: 1'b1, switch_18_p2[3], switch_18_p2[3]
  // Switch switch_14: pin names not known; wires that end beside it: 1'b1, switch_18_p2[2], switch_18_p2[2]
  Pull_Resistor pull_resistor_13 (.node(switch_18_p2[3]));
  Pull_Resistor pull_resistor_14 (.node(switch_18_p2[2]));
  and and_3 (and_3_out, not_2_out, switch_1_p2);
  not not_2 (not_2_out, w65c02s_simple_1_p5);
  assign controlled_buffer_1_out = switch_1_p2 ? w65c02s_simple_1_p7 : 16'bz;  // Controlled_Buffer controlled_buffer_1
  assign w65c02s_simple_1_p6 = w65c02s_simple_1_p5 ? {controlled_buffer_3_out_2[7], controlled_buffer_3_out} : 8'bz;  // Controlled_Buffer controlled_buffer_2
  LED led_24 (.in(controlled_buffer_1_out[0]));
  not not_3 (not_3_out, switch_1_p2);
  // Switch switch_15: pin names not known; wires that end beside it: 1'b1, switch_25_p2[9]
  // Switch switch_16: pin names not known; wires that end beside it: 1'b1, switch_25_p2[8]
  Pull_Resistor pull_resistor_15 (.node(switch_25_p2[9]));
  // Switch switch_17: pin names not known; wires that end beside it: 1'b1, switch_18_p2[1], switch_18_p2[1]
  // Switch switch_18: pin names not known; wires that end beside it: 1'b1, switch_18_p2[0], switch_18_p2[0]
  Pull_Resistor pull_resistor_16 (.node(switch_18_p2[1]));
  assign {controlled_buffer_3_out_2[7], controlled_buffer_3_out} = and_3_out ? w65c02s_simple_1_p6 : 8'bz;  // Controlled_Buffer controlled_buffer_3
  not not_4 (not_4_out, switch_1_p2);
  assign controlled_buffer_1_out = not_3_out ? switch_25_p2 : 16'bz;  // Controlled_Buffer controlled_buffer_4
  // Switch switch_19: pin names not known; wires that end beside it: 1'b1, switch_25_p2[7]
  Pull_Resistor pull_resistor_17 (.node(switch_25_p2[8]));
  Pull_Resistor pull_resistor_18 (.node(switch_25_p2[7]));
  Pull_Resistor pull_resistor_19 (.node(switch_18_p2[0]));
  assign controlled_buffer_5_out = switch_1_p2 ? w65c02s_simple_1_p5 : 1'bz;  // Controlled_Buffer controlled_buffer_5
  assign controlled_buffer_5_out = not_4_out ? not_5_out : 1'bz;  // Controlled_Buffer controlled_buffer_6
  not not_5 (not_5_out, switch_2_p2);
  // Switch switch_20: pin names not known; wires that end beside it: 1'b1, switch_25_p2[6]
  // Switch switch_21: pin names not known; wires that end beside it: 1'b1, switch_25_p2[5]
  Pull_Resistor pull_resistor_20 (.node(switch_25_p2[6]));
  Pull_Resistor pull_resistor_21 (.node(switch_25_p2[5]));
  // Switch switch_22: pin names not known; wires that end beside it: 1'b1, switch_25_p2[4]
  Pull_Resistor pull_resistor_22 (.node(switch_25_p2[4]));
  or or_1 (or_1_out, controlled_buffer_1_out[15], controlled_buffer_1_out[14], controlled_buffer_1_out[13]);
  and and_4 (and_4_out, controlled_buffer_1_out[15], controlled_buffer_1_out[14], controlled_buffer_1_out[13]);
  not not_6 (not_6_out, or_1_out);
  and and_5 (and_5_out, not_6_out, controlled_buffer_5_out);
  and and_6 (and_6_out, not_6_out, not_7_out);
  not not_7 (not_7_out, controlled_buffer_5_out);
  // Switch switch_23: pin names not known; wires that end beside it: 1'b1, switch_25_p2[3]
  // Switch switch_24: pin names not known; wires that end beside it: 1'b1, switch_25_p2[2]
  Pull_Resistor pull_resistor_23 (.node(switch_25_p2[3]));
  Pull_Resistor pull_resistor_24 (.node(switch_25_p2[2]));
  assign {controlled_buffer_3_out_2[7], controlled_buffer_3_out} = switch_1_p2 ? controlled_buffer_10_out : 8'bz;  // Controlled_Buffer controlled_buffer_7
  RAM #(.addrWidth(15)) ram_1 (
    .addr(controlled_buffer_1_out[14:0]), .we(and_6_out), .oe(and_5_out), .clk(clock_1_out),
    .din({controlled_buffer_3_out_2[7], controlled_buffer_3_out}), .dout(ram_1_dout));
  ROM #(.addrWidth(13)) rom_1 (.addr(controlled_buffer_1_out[12:0]), .data(rom_1_data));
  Comparator #(.width(16)) comparator_1 (
    .a(controlled_buffer_1_out), .b(16'h8000), .eq(comparator_1_eq));  // open: gt, lt
  Comparator #(.width(16)) comparator_2 (
    .a(controlled_buffer_1_out), .b(16'h8001), .eq(comparator_2_eq));  // open: gt, lt
  // Switch switch_25: pin names not known; wires that end beside it: 1'b1, switch_25_p2[0]
  // Switch switch_26: pin names not known; wires that end beside it: 1'b1, switch_25_p2[1]
  Pull_Resistor pull_resistor_25 (.node(switch_25_p2[1]));
  and and_7 (and_7_out, controlled_buffer_5_out, comparator_2_eq);
  assign {controlled_buffer_3_out_2[7], controlled_buffer_3_out} = not_3_out ? switch_18_p2 : 8'bz;  // Controlled_Buffer controlled_buffer_8
  Pull_Resistor pull_resistor_26 (.node(switch_25_p2[0]));
  and and_8 (and_8_out, comparator_1_eq, not_7_out);
  and and_9 (and_9_out, and_4_out, controlled_buffer_5_out);
  Keyboard #(.trigger("falling")) keyboard_1 (
    .clk(clock_1_out), .re(and_7_out), .data(keyboard_1_data));  // open: clr, avail
  assign {controlled_buffer_3_out_2[7], controlled_buffer_3_out} = and_7_out ? {1'b0, keyboard_1_data} : 8'bz;  // Controlled_Buffer controlled_buffer_9
  TTY #(.cols(80), .rows(25)) tty_1 (.data(controlled_buffer_3_out), .clk(clock_1_out), .we(and_8_out));  // open: clr
  assign controlled_buffer_10_out = and_5_out ? ram_1_dout : 8'bz;  // Controlled_Buffer controlled_buffer_10
  assign controlled_buffer_10_out = and_9_out ? rom_1_data : 8'bz;  // Controlled_Buffer controlled_buffer_11

  // Notes on the sheet:
  //   Enable CPU
  //   Enable Write
  //   Address
  //   Data
  //   contents of rom_1 (hex, n*v repeats v):
  //   ad fe 7f cd ff 7f d0 4 c9 0 f0 3 6c fe 7f a9 ba 85 2 a9 e1 85 3 20 1d e0 4c 2b e0 a0 0 b1 2 f0 7 8d
  //   0 80 c8 4c 1f e0 60 20 ad e1 a9 0 85 35 85 36 85 37 85 38 85 39 85 3a a9 3f 8d 0 80 a0 0 ad 1 80 f0
  //   fb c9 a f0 1c c9 8 f0 e 99 4 0 8d 0 80 c8 c0 30 f0 d0 4c 43 e0 8d 0 80 88 10 df c8 4c 43 e0 8d 0 80
  //   a0 0 20 a8 e1 c9 20 f0 f9 c9 72 f0 b c9 77 f0 42 c9 65 f0 68 4c 2b e0 20 ee e0 a9 1 85 3d a5 35 85
  //   3b a5 36 85 3c e0 0 f0 7 20 ee e0 a5 35 85 3d a0 0 b1 3b aa 98 48 8a 20 52 e1 aa 68 a8 8a a9 20 8d 0
  //   80 c8 c4 3d d0 e9 a9 a 8d 0 80 4c 2b e0 20 ee e0 e0 0 d0 3 4c 2b e0 a5 35 85 3b a5 36 85 3c 84 3d a4
  //   3d 20 ee e0 84 3d a0 0 a5 35 91 3b e6 3b e0 0 d0 ed 4c 2b e0 20 ee e0 6c 35 0 a9 0 85 35 85 36 b9 4
  //   0 c9 20 d0 6 20 a8 e1 4c ee e0 a9 0 a2 0 20 a8 e1 c9 0 f0 42 c9 20 f0 3c c9 30 30 3b f0 9 c9 61 30
  //   17 f0 8 4c 29 e1 a9 0 4c 34 e1 a9 a 4c 34 e1 18 e9 61 69 a 4c 34 e1 38 e9 30 6 35 26 36 6 35 26 36 6
  //   35 26 36 6 35 26 36 18 5 35 85 35 4c 1 e1 a2 1 60 4c 2b e0 a2 1 a0 0 84 3a 84 37 84 38 c9 0 f0 3f 4a
  //   66 3a 4a 66 3a 4a 66 3a 4a 66 3a 18 66 3a 66 3a 66 3a 66 3a 18 a8 a5 3a c9 a 30 8 e9 a 18 69 41 4c
  //   87 e1 69 30 95 37 a9 0 85 3a ca 98 e0 ff d0 cd a9 37 85 2 a9 0 85 3 20 1d e0 60 a9 30 8d 0 80 8d 0
  //   80 60 b9 4 0 c8 60 a0 0 a9 0 99 4 0 c8 c0 30 d0 f8 60 4e 6f 20 70 72 6f 67 72 61 6d 20 66 6f 75 6e
  //   64 20 69 6e 20 52 41 4d 20 28 56 65 63 74 6f 72 20 24 37 66 66 65 20 3d 20 24 4*30 29 2e d a 44 65
  //   66 61 75 6c 74 69 6e 67 20 74 6f 20 6d 61 63 68 69 6e 65 20 6c 61 6e 67 75 61 67 65 20 6d 6f 6e 69
  //   74 6f 72 2e d a 7657*0 e0
endmodule
